# Fritzing sketch ESP8266-programmer (saved by Fritzing 0.9.3b)
circuit board: 5cm x 5cm
breadboards: 1

parts:
  part = female pin header, 2 pins [form="♀ (female)"]
  part_2 = female pin header, 2 pins [form="♀ (female)"]
  part_3 = female pin header, 2 pins [form="♀ (female)"]
  part_4 = female pin header, 2 pins [form="♀ (female)"]
  U1 = Voltage Regulator - 3.3V [package="TO220 [THT]"]
  J5 = female pin header, 2 pins [form="♀ (female)"]
  J6 = female pin header, 2 pins [form="♀ (female)"]
  part_5 = female pin header, 2 pins [form="♀ (female)"]
  part_6 = female pin header, 2 pins [form="♀ (female)"]
  RESET = Pushbutton [package="[THT]"]
  R1 = Resistor [tolerance=±5% resistance=3.3k package=THT]
  R2 = Resistor [tolerance=±5% resistance=3.3k package=THT]
  R3 = Resistor [tolerance=±5% resistance=330 package=THT]
  R4 = Resistor [tolerance=±5% resistance=3.3k package=THT]
  R5 = Resistor [tolerance=±5% resistance=3.3k package=THT]
  PROG = Toggle Switch [package=THT]
  C1 = Electrolytic Capacitor [capacitance=0.1mF package="100 mil [THT, electrolytic]"]
  C2 = Electrolytic Capacitor [capacitance=0.1mF package="100 mil [THT, electrolytic]"]
  part_7 = female pin header, 2 pins [form="♀ (female)"]

nets:
  N1: part.pin1, part_6.pin2, R3.Pin_1
  N2: part.pin2, part_5.pin1, R5.Pin_1, PROG.COM
  N3: part_2.pin1, part_6.pin1, R4.Pin_1
  N4: part_2.pin2, U1.input_voltage, J6.pin2, RESET.Pin_3, RESET.Pin_4, PROG.L1, C1.-, C2.-, part_7.pin2
  N5: part_3.pin1, U1.GND, R1.Pin_0, R2.Pin_0, R4.Pin_0, R5.Pin_0, C1.+, part_7.pin1
  N6: part_3.pin2, RESET.Pin_1, RESET.Pin_2, R1.Pin_1
  N7: part_4.pin1, R2.Pin_1
  N8: part_4.pin2, J6.pin1, part_5.pin2
  N9: U1.output_voltage, J5.pin1, C2.+
  N10: J5.pin2, R3.Pin_0

notes:
  vin
  rx
  tx
  gnd
  GPIO0
  GPIO1
  GPIO2
  GPIO3
  3.3v
  GND
  N. Whyte
  ESP8266-Breakout
  V1.2016.11
  VCC
