# Fritzing sketch Garagev2 (saved by Fritzing 0.9.3b)
circuit board: 5cm x 5cm
breadboards: 1

parts:
  part = Camdenboss CTB0158-2 [part_number=CTB0158-2 package=THT]
  part_2 = Camdenboss CTB0158-2 [part_number=CTB0158-2 package=THT]
  part_3 = Camdenboss CTB0158-3 [part_number=CTB0158-3 package=THT]
  3_3V_REG = Voltage Regulator - 3.3V [part_number=LM1117T package="TO220 [THT]"]
  part_4 = Electrolytic Capacitor [capacitance=10µF package="100 mil [THT, electrolytic]"]
  part_5 = Electrolytic Capacitor [capacitance=10µF package="100 mil [THT, electrolytic]"]
  part_6 = female pin header, 2 pins [form="♀ (female)"]
  part_7 = female pin header, 2 pins [form="♀ (female)"]
  part_8 = female pin header, 2 pins [form="♀ (female)"]
  part_9 = female pin header, 2 pins [form="♀ (female)"]
  part_10 = Resistor [tolerance=±5% resistance=3.3k package=THT]
  part_11 = Resistor [tolerance=±5% resistance=3.3k package=THT]
  part_12 = Resistor [tolerance=±5% resistance=3.3k package=THT]
  part_13 = Resistor [tolerance=±5% resistance=3.3k package=THT]
  part_14 = Resistor [tolerance=±5% resistance=3.3k package=THT]
  R6_1K = Resistor [tolerance=±5% resistance=1k package=THT]
  part_15 = PNP-Transistor [package="TO92 [THT]"]
  DEBUG = female pin header, 2 pins [form="♀ (female)"]

nets:
  N1: part.pin1, part_2.pin1, part_3.pin2, 3_3V_REG.input_voltage, part_4.-, part_5.-, part_9.pin2, R6_1K.Pin_0, part_15.E, DEBUG.pin1
  N2: part.pin2, part_2.pin2, 3_3V_REG.output_voltage, part_4.+
  N3: part_3.pin1, part_15.C
  N4: part_3.pin3, part_6.pin1, part_12.Pin_1
  N5: 3_3V_REG.GND, part_5.+, part_7.pin1, part_10.Pin_0, part_11.Pin_0, part_12.Pin_0, part_13.Pin_0, part_14.Pin_0
  N6: part_6.pin2, part_14.Pin_1
  N7: part_7.pin2, part_10.Pin_1
  N8: part_8.pin1, part_11.Pin_1
  N9: part_8.pin2, DEBUG.pin2
  N10: part_9.pin1, part_13.Pin_1
  N11: R6_1K.Pin_1, part_15.B

notes:
  GND
  TX
  SENSE
  TRIGGER
  +V
  Vin
  V2.2016.12
  hc-relay
  N. Whyte
