# Fritzing sketch blindkit (saved by Fritzing 0.9.3b)
circuit board: 5cm x 5cm
breadboards: 1

parts:
  J1 = Camdenboss CTB0158-2 [part_number="CTB0158-1 Vin" package=THT]
  C1 = Electrolytic Capacitor [capacitance=10µF package="100 mil [THT, electrolytic]"]
  C2 = Electrolytic Capacitor [capacitance=10µF package="100 mil [THT, electrolytic]"]
  R1 = Resistor [tolerance=±5% resistance=3.3k package=THT]
  R2 = Resistor [tolerance=±5% resistance=3.3k package=THT]
  R4 = Resistor [tolerance=±5% resistance=3.3k package=THT]
  R5 = Resistor [tolerance=±5% resistance=3.3k package=THT]
  DEBUG = female pin header, 2 pins [form="♀ (female)"]
  U1 = ESP8266 WiFi Module [part_number=ESP8266]
  U2 = Voltage Regulator - 3.3V [part_number=LM1117T package="TO220 [THT]"]
  U3 = FS1000A - 433Mhz RF Transmitter [package=THT]

nets:
  GND: J1.pin1, C1.-, C2.-, DEBUG.pin1, U1.GND, U2.GND, U3.GND
  N1: J1.pin2, C1.+, U2.input_voltage
  VCC: C2.+, R1.Pin_0, R2.Pin_0, R4.Pin_0, R5.Pin_0, U1.VCC, U2.output_voltage, U3.VCC
  N2: R1.Pin_1, U1.RST
  N3: R2.Pin_1, U1.CH_PD
  N4: R4.Pin_1, U1.GPIO_2
  N5: R5.Pin_1, U1.GPIO_0
  N6: DEBUG.pin2, U1.TXD
  N7: U1.RXD, U3.DATA

notes:
  GND
  TX
  Vin
  V1.2017.08
  blindkit
  N. Whyte

custom parts:
  ESP8266 WiFi Module: Generic WiFi Module based on the ESP8266 with onboard PCB antenna and UART communications
  Voltage Regulator - 3.3V: 3.3V DC Voltage Regulator
  FS1000A - 433Mhz RF Transmitter: This is 433Mhz RF transmitter with receiver kit for Arduino ARM MCU wireless Application environment: Remote control switch, receiver module, motorcycles, automobile anti-theft products, home security products, electric doors, shutter doors, windows, remote control socket, remote control LED, remote audio remote control electric doors, garage door remote control, remote control retractable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
